// Logisim project 0-59 Counter (copy).circ as structural Verilog: 8 circuits, main circuit main
module main (
  input  Clear,
  input  Select,
  input  clock,
  input  [3:0] parallelt,
  input  [2:0] parallelo,
  output [3:0] X1,
  output [3:0] X0
);

  wire _7_Segment_Decoder_2_a, _7_Segment_Decoder_2_b, _7_Segment_Decoder_2_c, _7_Segment_Decoder_2_d,
       _7_Segment_Decoder_2_e, _7_Segment_Decoder_2_f, _7_Segment_Decoder_2_g, _7_Segment_Decoder_a,
       _7_Segment_Decoder_b, _7_Segment_Decoder_c, _7_Segment_Decoder_d, _7_Segment_Decoder_e,
       _7_Segment_Decoder_f, _7_Segment_Decoder_g, AND_2_out, AND_3_out, AND_4_out, AND_out, not_1_out,
       not_2_out, not_3_out, not_4_out, not_5_out, OR_out;

  Up_Down_Decade_Counter Decade_Counter (
    .Clear(Clear), .Select(Select), .Clock(clock), .Output(X0), .parallel(parallelt));
  not not_1 (not_1_out, Select);
  and AND (AND_out, not_1_out, not_2_out);
  not not_2 (not_2_out, X0[0]);
  not not_3 (not_3_out, X0[1]);
  not not_4 (not_4_out, X0[2]);
  and AND_2 (AND_2_out, not_3_out, not_4_out, not_5_out);
  not not_5 (not_5_out, X0[3]);
  and AND_3 (AND_3_out, Select, X0[0], X0[3]);
  and AND_4 (AND_4_out, AND_out, AND_2_out);
  or OR (OR_out, AND_3_out, AND_4_out);
  _7_Segment_Decoder _7_Segment_Decoder (
    .X({1'b0, X1[2:0]}), .A(_7_Segment_Decoder_a), .B(_7_Segment_Decoder_b), .C(_7_Segment_Decoder_c),
    .D(_7_Segment_Decoder_d), .E(_7_Segment_Decoder_e), .F(_7_Segment_Decoder_f), .G(_7_Segment_Decoder_g));
  Up_Down_Mod_6_Counter up_down_mod_6_counter_1 (
    .Clear(Clear), .Select(Select), .Clock(OR_out), .Output(X1[2:0]), .parallel(parallelo));
  _7_Segment_Display u_7_segment_display_1 (
    .g(_7_Segment_Decoder_g), .f(_7_Segment_Decoder_f), .a(_7_Segment_Decoder_a), .b(_7_Segment_Decoder_b),
    .e(_7_Segment_Decoder_e), .d(_7_Segment_Decoder_d), .c(_7_Segment_Decoder_c));  // open: dp
  _7_Segment_Decoder _7_Segment_Decoder_2 (
    .X(X0), .A(_7_Segment_Decoder_2_a), .B(_7_Segment_Decoder_2_b), .C(_7_Segment_Decoder_2_c),
    .D(_7_Segment_Decoder_2_d), .E(_7_Segment_Decoder_2_e), .F(_7_Segment_Decoder_2_f),
    .G(_7_Segment_Decoder_2_g));
  _7_Segment_Display u_7_segment_display_2 (
    .g(_7_Segment_Decoder_2_g), .f(_7_Segment_Decoder_2_f), .a(_7_Segment_Decoder_2_a),
    .b(_7_Segment_Decoder_2_b), .e(_7_Segment_Decoder_2_e), .d(_7_Segment_Decoder_2_d),
    .c(_7_Segment_Decoder_2_c));  // open: dp

  assign X1[3] = 1'b0;

  // Notes on the sheet:
  //   S (0 if UP / 1 if DOWN)
  //   0-59 Counter
endmodule

module Up_Down_Mod_6_Counter (
  input  Clear,
  input  Select,
  input  Clock,
  input  [2:0] parallel,
  output [2:0] Output
);

  wire AND_2_out, AND_out, FF_0_qn, FF_1_qn, FF_2_qn, not_1_out, OR_2_out, OR_3_out, OR_4_out, OR_out,
       XOR_out;

  not not_1 (not_1_out, Select);
  and AND (AND_out, Select, FF_0_qn, Output[2]);
  and AND_2 (AND_2_out, not_1_out, Output[0], FF_2_qn);
  J_K_Flip_Flop FF_0 (
    .J(1'b1), .clk(Clock), .K(1'b1), .Q(Output[0]), .Qn(FF_0_qn), .preset(parallel[2]), .reset(Clear));  // open: en
  xor XOR (XOR_out, Output[0], Select);
  or OR (OR_out, AND_2_out, AND_out);
  and OR_2 (OR_2_out, not_1_out, Output[0], Output[1]);
  J_K_Flip_Flop FF_1 (
    .J(OR_out), .clk(Clock), .K(XOR_out), .Q(Output[1]), .Qn(FF_1_qn), .preset(parallel[1]), .reset(Clear));  // open: en
  or OR_3 (OR_3_out, OR_2_out, OR_4_out);
  and OR_4 (OR_4_out, Select, FF_1_qn, FF_0_qn);
  J_K_Flip_Flop FF_2 (
    .J(OR_3_out), .clk(Clock), .K(XOR_out), .Q(Output[2]), .Qn(FF_2_qn), .preset(parallel[0]), .reset(Clear));  // open: en

  // Notes on the sheet:
  //   S (0 if UP / 1 if DOWN)
  //   Mod-6 Counter
endmodule

module Up_Down_Decade_Counter (
  input  Clear,
  input  Select,
  input  Clock,
  input  [3:0] parallel,
  output [3:0] Output
);

  wire AND_2_out, AND_3_out, AND_4_out, AND_5_out, AND_6_out, AND_7_out, AND_8_out, AND_9_out, AND_10_out,
       AND_11_out, AND_out, FF_0_qn, FF_1_qn, FF_3_qn, FF_4_qn, not_1_out, OR_2_out, OR_3_out, OR_4_out,
       OR_out, XOR_out;

  not not_1 (not_1_out, Select);
  and AND (AND_out, not_1_out, FF_4_qn, Output[0]);
  J_K_Flip_Flop FF_0 (
    .J(1'b1), .clk(Clock), .K(1'b1), .Q(Output[0]), .Qn(FF_0_qn), .preset(parallel[3]), .reset(Clear));  // open: en
  or OR (OR_out, AND_out, AND_2_out);
  and AND_2 (AND_2_out, Select, FF_0_qn, OR_2_out);
  and AND_3 (AND_3_out, not_1_out, Output[0], Output[1]);
  or OR_2 (OR_2_out, Output[3], Output[2]);
  J_K_Flip_Flop FF_1 (
    .J(OR_out), .clk(Clock), .K(XOR_out), .Q(Output[1]), .Qn(FF_1_qn), .preset(parallel[2]), .reset(Clear));  // open: en
  and AND_4 (AND_4_out, Select, FF_0_qn, FF_1_qn);
  xor XOR (XOR_out, Output[0], Select);
  or OR_3 (OR_3_out, AND_3_out, AND_5_out);
  and AND_5 (AND_5_out, Select, Output[3], FF_0_qn);
  and AND_6 (AND_6_out, Output[0], not_1_out, Output[1]);
  or OR_4 (OR_4_out, AND_6_out, AND_4_out);
  and AND_7 (AND_7_out, not_1_out, AND_8_out);
  and AND_8 (AND_8_out, Output[0], Output[1], Output[2]);
  J_K_Flip_Flop FF_3 (
    .J(OR_3_out), .clk(Clock), .K(OR_4_out), .Q(Output[2]), .Qn(FF_3_qn), .preset(parallel[1]), .reset(Clear));  // open: en
  and AND_9 (AND_9_out, FF_0_qn, FF_1_qn, FF_3_qn);
  and AND_10 (AND_10_out, Select, AND_9_out);
  or AND_11 (AND_11_out, AND_7_out, AND_10_out);
  J_K_Flip_Flop FF_4 (
    .J(AND_11_out), .clk(Clock), .K(XOR_out), .Q(Output[3]), .Qn(FF_4_qn), .preset(parallel[0]), .reset(Clear));  // open: en

  // Notes on the sheet:
  //   S (0 if UP / 1 if DOWN)
  //   Decade Counter
endmodule

module _7_Segment_Decoder (
  input  [3:0] X,
  output A,
  output B,
  output C,
  output D,
  output E,
  output F,
  output G
);

  wire and_1_out, and_2_out, and_3_out, and_4_out, and_5_out, and_6_out, and_7_out, and_8_out, and_9_out,
       and_10_out, and_11_out, and_12_out, and_13_out, and_14_out, and_15_out, and_16_out, and_17_out,
       not_1_out, not_2_out, not_3_out, not_4_out, not_5_out, not_6_out, not_7_out, not_8_out, not_9_out,
       not_10_out, not_11_out, not_12_out, not_13_out, not_14_out, not_15_out, not_16_out, not_17_out,
       not_18_out, not_19_out, not_20_out, not_21_out, or_1_out, or_2_out, or_3_out, or_4_out, or_6_out,
       or_8_out, or_9_out, or_10_out, or_11_out, or_14_out, or_15_out;

  not not_1 (not_1_out, X[2]);
  not not_2 (not_2_out, X[0]);
  not not_3 (not_3_out, X[1]);
  not not_4 (not_4_out, X[0]);
  not not_5 (not_5_out, X[1]);
  not not_6 (not_6_out, X[2]);
  not not_7 (not_7_out, X[0]);
  not not_8 (not_8_out, X[2]);
  not not_9 (not_9_out, X[1]);
  not not_10 (not_10_out, X[2]);
  not not_11 (not_11_out, X[0]);
  not not_12 (not_12_out, X[0]);
  not not_13 (not_13_out, X[1]);
  not not_14 (not_14_out, X[0]);
  not not_15 (not_15_out, X[1]);
  not not_16 (not_16_out, X[0]);
  not not_17 (not_17_out, X[2]);
  not not_18 (not_18_out, X[1]);
  not not_19 (not_19_out, X[0]);
  and and_1 (and_1_out, not_1_out, not_2_out);
  and and_2 (and_2_out, X[2], X[0]);
  not not_20 (not_20_out, X[2]);
  and and_3 (and_3_out, not_3_out, not_4_out);
  or or_1 (or_1_out, not_5_out, X[0]);
  and and_4 (and_4_out, not_6_out, not_7_out);
  and and_5 (and_5_out, not_8_out, X[1]);
  not not_21 (not_21_out, X[0]);
  and and_6 (and_6_out, X[2], not_9_out);
  and and_7 (and_7_out, not_10_out, not_11_out);
  and and_8 (and_8_out, X[1], not_12_out);
  and and_9 (and_9_out, not_13_out, not_14_out);
  and and_10 (and_10_out, X[2], not_15_out);
  and and_11 (and_11_out, X[2], not_16_out);
  and and_12 (and_12_out, not_17_out, X[1]);
  and and_13 (and_13_out, X[2], not_18_out);
  and and_14 (and_14_out, X[2], not_19_out);
  or or_2 (or_2_out, and_1_out, X[1]);
  or or_3 (or_3_out, and_2_out, X[3]);
  or or_4 (or_4_out, not_20_out, and_3_out);
  and and_15 (and_15_out, X[1], X[0]);
  or or_5 (C, or_1_out, X[2]);
  or or_6 (or_6_out, and_4_out, and_5_out);
  and and_16 (and_16_out, X[1], not_21_out);
  and and_17 (and_17_out, and_6_out, X[0]);
  or or_7 (E, and_7_out, and_8_out);
  or or_8 (or_8_out, and_9_out, and_10_out);
  or or_9 (or_9_out, and_11_out, X[3]);
  or or_10 (or_10_out, and_12_out, and_13_out);
  or or_11 (or_11_out, and_14_out, X[3]);
  or or_12 (A, or_2_out, or_3_out);
  or or_13 (B, or_4_out, and_15_out);
  or or_14 (or_14_out, or_6_out, and_16_out);
  or or_15 (or_15_out, and_17_out, X[3]);
  or or_16 (F, or_8_out, or_9_out);
  or or_17 (G, or_10_out, or_11_out);
  or or_18 (D, or_14_out, or_15_out);
endmodule

module _0_23_Counter (
  input  Clear,
  input  Clock,
  input  [3:0] parallelo,
  input  [1:0] parallelt,
  output [3:0] X1,
  output [3:0] X0
);

  wire AND_2_out, AND_3_out, AND_4_out, AND_5_out, AND_6_out, AND_7_out, AND_8_out, AND_out, not_1_out,
       not_2_out, not_3_out, not_4_out, not_5_out, not_6_out, or_1_out;

  or or_1 (or_1_out, Clear, AND_out);
  Up_Down_Decade_Counter up_down_decade_counter_1 (
    .Clear(or_1_out), .Select(1'b0), .Clock(Clock), .Output(X0), .parallel(parallelo));
  and AND (AND_out, Clock, AND_2_out);
  and AND_2 (AND_2_out, AND_8_out, AND_6_out, AND_3_out);
  and AND_3 (AND_3_out, not_2_out, not_1_out);
  not not_1 (not_1_out, 1'b0);
  and AND_4 (AND_4_out, not_1_out, not_2_out);
  not not_2 (not_2_out, X0[0]);
  not not_3 (not_3_out, X0[1]);
  not not_4 (not_4_out, X0[2]);
  and AND_5 (AND_5_out, not_3_out, not_4_out, not_5_out);
  not not_5 (not_5_out, X0[3]);
  and AND_6 (AND_6_out, X0[2], not_5_out);
  and AND_7 (AND_7_out, AND_4_out, AND_5_out);
  and AND_8 (AND_8_out, not_6_out, X1[1]);
  not not_6 (not_6_out, X1[0]);
  Mod_3_Counter mod_3_counter_1 (.Clear(Clear), .Clock(AND_7_out), .Output(X1), .parallel(parallelt));

  // Notes on the sheet:
  //   0-23 Counter
endmodule

module Mod_3_Counter (
  input  Clear,
  input  Clock,
  input  [1:0] parallel,
  output [3:0] Output
);

  wire j_k_ff_2_qn;

  J_K_Flip_Flop j_k_ff_1 (
    .J(j_k_ff_2_qn), .clk(Clock), .K(1'b1), .Q(Output[0]), .preset(parallel[1]), .reset(Clear));  // open: Qn, en
  J_K_Flip_Flop j_k_ff_2 (
    .J(Output[0]), .clk(Clock), .K(1'b1), .Q(Output[1]), .Qn(j_k_ff_2_qn), .preset(parallel[0]), .reset(Clear));  // open: en

  assign Output[3:2] = 2'b00;
endmodule

module clock (
  input  clear,
  input  [3:0] in_2,
  input  [1:0] in_3,
  input  [3:0] in_4,
  input  [2:0] in_5,
  input  [3:0] in_6,
  input  [2:0] in_7
);

  wire clock_out, COMB_2_output, COMB_output;
  wire [3:0] main_1_x0, main_1_x1, main_2_x0, main_2_x1, n0_23_counter_1_x0, n0_23_counter_1_x1;

  Clock clock (.out(clock_out));
  main main_1 (
    .Clear(clear), .Select(1'b0), .clock(clock_out), .parallelt(in_4), .parallelo(in_5), .X1(main_1_x1),
    .X0(main_1_x0));
  comb COMB (.\input (main_1_x1), .\output (COMB_output));
  main main_2 (
    .Clear(clear), .Select(1'b0), .clock(COMB_output), .parallelt(in_6), .parallelo(in_7), .X1(main_2_x1),
    .X0(main_2_x0));
  comb COMB_2 (.\input (main_2_x1), .\output (COMB_2_output));
  Hex_Digit_Display hex_digit_display_1 (.value(n0_23_counter_1_x1));  // open: dp
  Hex_Digit_Display hex_digit_display_2 (.value(n0_23_counter_1_x0));  // open: dp
  _0_23_Counter u_0_23_counter_1 (
    .Clear(clear), .Clock(COMB_2_output), .X1(n0_23_counter_1_x1), .X0(n0_23_counter_1_x0), .parallelo(in_2),
    .parallelt(in_3));
  Hex_Digit_Display hex_digit_display_3 (.value(main_2_x1));  // open: dp
  Hex_Digit_Display hex_digit_display_4 (.value(main_2_x0));  // open: dp
  Hex_Digit_Display hex_digit_display_5 (.value(main_1_x1));  // open: dp
  Hex_Digit_Display hex_digit_display_6 (.value(main_1_x0));  // open: dp

  // Notes on the sheet:
  //   Prallel load for second's hand
  //   mod 60
  //   Parallel load for minute's hand
  //   24 Hour Clock
  //   mod 60
  //   HOURS
  //   mod 24 
  //   Parallel load for hour's hand
  //   MINUTES
  //   SECONDS
endmodule

module comb (
  input  [3:0] \input ,
  output \output 
);

  wire and_1_out, and_2_out, not_1_out, not_2_out, not_3_out, not_4_out;

  not not_1 (not_1_out, \input [3]);
  not not_2 (not_2_out, \input [1]);
  not not_3 (not_3_out, \input [2]);
  and and_1 (and_1_out, not_1_out, not_3_out);
  and and_2 (and_2_out, not_2_out, not_4_out);
  and and_3 (\output , and_1_out, and_2_out);
  not not_4 (not_4_out, \input [0]);
endmodule
